// Logisim project cpu.circ as structural Verilog: 1 circuit, main circuit cpu
module cpu (
  input  clk,
  input  [31:0] Instruction,
  input  [31:0] MemReadData,
  output [31:0] MemAddress,
  output [31:0] ProgramCounter,
  output [31:0] ra,
  output [31:0] sp,
  output [31:0] t0,
  output [31:0] t1,
  output [31:0] t2,
  output [31:0] s0,
  output [31:0] s1,
  output [31:0] a0,
  output [3:0] MemWriteMask,
  output [31:0] MemWriteData
);

  wire ASel, BrEq, BrLt, BrUn, BSel, EXASEL, EXBRUN, EXBSEL, EXPCSEL, MAMEMEN, MemEn, PCSel, register_2_q,
       register_16_q, register_17_q, register_18_q, RegWEn, WBPCSEL, WBREGWEN;
  wire [1:0] register_1_q, register_8_q, WBSel, WBWBSEL;
  wire [2:0] EXIMMSEL, ImmSel;
  wire [3:0] ALUSel, EXALUSEL;
  wire [31:0] A_Value, adder_1_out, ALUResult, B_Value, DataToReg, EXINS, EXPC, EXRD1, EXRD2, IDINS, IDPC_q,
       immedimate, MAINS, MAPC, MARD2, multiplexer_2_out, PCPlus4, PCValue, ReadData1, ReadData2, WBDATA,
       WBData_t, WBINS;

  Register #(.width(32)) PC (.D(PCValue), .clk(clk), .Q(ProgramCounter));  // open: en, clr
  Adder #(.width(32)) adder_1 (.a(ProgramCounter), .b(32'h4), .out(adder_1_out));  // open: cin, cout
  Multiplexer #(.width(32)) multiplexer_1 (.in0(adder_1_out), .in1(ALUResult), .out(PCValue), .sel(WBPCSEL));
  Register #(.width(2)) register_1 (.D(WBSel), .clk(clk), .Q(register_1_q));  // open: en, clr
  Register #(.width(1)) register_2 (.D(MemEn), .clk(clk), .Q(register_2_q));  // open: en, clr
  Register #(.width(4)) register_3 (.D(ALUSel), .clk(clk), .Q(EXALUSEL));  // open: en, clr
  Register #(.width(3)) register_4 (.D(ImmSel), .clk(clk), .Q(EXIMMSEL));  // open: en, clr
  Register #(.width(1)) register_5 (.D(BrUn), .clk(clk), .Q(EXBRUN));  // open: en, clr
  Register #(.width(1)) register_6 (.D(ASel), .clk(clk), .Q(EXASEL));  // open: en, clr
  Register #(.width(1)) register_7 (.D(BSel), .clk(clk), .Q(EXBSEL));  // open: en, clr
  Register #(.width(2)) register_8 (.D(register_1_q), .clk(clk), .Q(register_8_q));  // open: en, clr
  Register #(.width(1)) register_9 (.D(register_2_q), .clk(clk), .Q(MAMEMEN));  // open: en, clr
  Register #(.width(2)) register_10 (.D(register_8_q), .clk(clk), .Q(WBWBSEL));  // open: en, clr
  control_logic control_logic_1 (
    .Instruction(IDINS), .BrEq(BrEq), .BrLt(BrLt), .PCSel(PCSel), .RegWEn(RegWEn), .ImmSel(ImmSel),
    .BrUn(BrUn), .ASel(ASel), .BSel(BSel), .ALUSel(ALUSel), .MemWEn(MemEn), .WBSel(WBSel));
  imm_gen imm_gen_1 (.Instruction(EXINS), .ImmSel(EXIMMSEL), .Immediate(immedimate));
  regfile regfile_1 (
    .ReadIndex1(IDINS[19:15]), .ReadIndex2(IDINS[24:20]), .WriteIndex(IDINS[11:7]), .WriteData(WBDATA),
    .RegWEn(WBREGWEN), .clk(clk), .ra(ra), .sp(sp), .t0(t0), .t1(t1), .t2(t2), .s0(s0), .s1(s1), .a0(a0),
    .ReadData1(ReadData1), .ReadData2(ReadData2));
  Multiplexer #(.width(32)) multiplexer_2 (.in0(Instruction), .in1(32'h13), .out(multiplexer_2_out), .sel(EXPCSEL));
  Register #(.width(32)) register_11 (.D(ALUResult), .clk(clk), .Q(MemAddress));  // open: en, clr
  Register #(.width(32)) register_12 (.D(WBData_t), .clk(clk), .Q(WBDATA));  // open: en, clr
  Register #(.width(32)) u_IDINS (.D(multiplexer_2_out), .clk(clk), .Q(IDINS));  // open: en, clr
  Register #(.width(32)) IDPC (.D(ProgramCounter), .clk(clk), .Q(IDPC_q));  // open: en, clr
  Register #(.width(32)) register_13 (.D(ReadData1), .clk(clk), .Q(EXRD1));  // open: en, clr
  Register #(.width(32)) register_14 (.D(ReadData2), .clk(clk), .Q(EXRD2));  // open: en, clr
  Register #(.width(32)) u_EXPC (.D(IDPC_q), .clk(clk), .Q(EXPC));  // open: en, clr
  Register #(.width(32)) register_15 (.D(EXRD2), .clk(clk), .Q(MARD2));  // open: en, clr
  alu alu_1 (.A(A_Value), .B(B_Value), .ALUSel(EXALUSEL), .ALUResult(ALUResult));
  branch_comp branch_comp_1 (.BrData1(EXRD1), .BrData2(EXRD2), .BrUn(EXBRUN), .BrEq(BrEq), .BrLt(BrLt));
  Register #(.width(32)) u_EXINS (.D(IDINS), .clk(clk), .Q(EXINS));  // open: en, clr
  Register #(.width(32)) u_MAINS (.D(EXINS), .clk(clk), .Q(MAINS));  // open: en, clr
  Register #(.width(32)) u_MAPC (.D(EXPC), .clk(clk), .Q(MAPC));  // open: en, clr
  Register #(.width(32)) u_WBINS (.D(MAINS), .clk(clk), .Q(WBINS));  // open: en, clr
  Multiplexer #(.width(32)) multiplexer_3 (.in0(EXRD2), .in1(immedimate), .out(B_Value), .sel(EXBSEL));
  Multiplexer #(.width(32)) multiplexer_4 (.in0(EXRD1), .in1(EXPC), .out(A_Value), .sel(EXASEL));
  Register #(.width(1)) register_16 (.D(RegWEn), .clk(clk), .Q(register_16_q));  // open: en, clr
  partial_store partial_store_1 (
    .Instruction(MAINS), .MemAddress(MemAddress), .DataFromReg(MARD2), .MemWEn(MAMEMEN),
    .MemWriteMask(MemWriteMask), .DataToMem(MemWriteData));
  partial_load partial_load_1 (
    .Instruction(MAINS), .MemAddress(MemAddress), .DataFromMem(MemReadData), .DataToReg(DataToReg));
  Register #(.width(1)) register_17 (.D(EXPCSEL), .clk(clk), .Q(register_17_q));  // open: en, clr
  Register #(.width(1)) register_18 (.D(register_16_q), .clk(clk), .Q(register_18_q));  // open: en, clr
  control_logic control_logic_2 (
    .Instruction(EXINS), .BrEq(BrEq), .BrLt(BrLt), .PCSel(EXPCSEL));  // open: RegWEn, ImmSel, BrUn, ASel, BSel, ALUSel, MemWEn, WBSel
  Register #(.width(1)) register_19 (.D(register_17_q), .clk(clk), .Q(WBPCSEL));  // open: en, clr
  Multiplexer #(.select(2), .width(32)) multiplexer_5 (
    .in0(DataToReg), .in1(MemAddress), .in2(PCPlus4), .out(WBData_t), .sel(WBWBSEL));  // open: in3
  Adder #(.width(32)) adder_2 (.a(MAPC), .b(32'h4), .out(PCPlus4));  // open: cin, cout
  Register #(.width(1)) register_20 (.D(register_18_q), .clk(clk), .Q(WBREGWEN));  // open: en, clr

  // Other names for the same wires on the sheet: rd[4:0] = IDINS[11:7]; rs1[4:0] = IDINS[19:15];
  //   rs2[4:0] = IDINS[24:20]; MAALU[31:0] = MemAddress

  // Notes on the sheet:
  //   To IMEM
  //   IMEM (do **NOT** move this)
  //   From IMEM
  //   Inputs/Outputs for testing. Do **NOT** move these.
  //   It is OK to move the PC, RegFile, ALU, MEM, Branch Comp, Imm Gen, Partial Load, Partial Store and Control Logic to wherever is most convenient for you when constructing your CPU, and to delete this text
  //   To DMEM
  //   DMEM (do **NOT** move this)
  //   From DMEM
endmodule
