// Logisim project regfile.circ as structural Verilog: 1 circuit, main circuit regfile
module regfile (
  input  [4:0] ReadIndex1,
  input  [4:0] ReadIndex2,
  input  [4:0] WriteIndex,
  input  [31:0] WriteData,
  input  RegWEn,
  input  clk,
  output [31:0] ra,
  output [31:0] sp,
  output [31:0] t0,
  output [31:0] t1,
  output [31:0] t2,
  output [31:0] s0,
  output [31:0] s1,
  output [31:0] a0,
  output [31:0] ReadData1,
  output [31:0] ReadData2
);

  wire WE1, WE2, WE3, WE4, WE5, WE6, WE7, WE8, WE9, WE10, WE11, WE12, WE13, WE14, WE15, WE16, WE17, WE18,
       WE19, WE20, WE21, WE22, WE23, WE24, WE25, WE26, WE27, WE28, WE29, WE30, WE31;
  wire [31:0] x3Out, x4Out, x11Out, x12Out, x13Out, x14Out, x15Out, x16Out, x17Out, x18Out, x19Out, x20Out,
       x21Out, x22Out, x23Out, x24Out, x25Out, x26Out, x27Out, x28Out, x29Out, x30Out, x31Out;

  Register #(.width(32)) x6 (.D(WriteData), .en(WE6), .clk(clk), .Q(t1));  // open: clr
  Register #(.width(32)) x9 (.D(WriteData), .en(WE9), .clk(clk), .Q(s1));  // open: clr
  Register #(.width(32)) x12 (.D(WriteData), .en(WE12), .clk(clk), .Q(x12Out));  // open: clr
  Register #(.width(32)) x15 (.D(WriteData), .en(WE15), .clk(clk), .Q(x15Out));  // open: clr
  Register #(.width(32)) x21 (.D(WriteData), .en(WE21), .clk(clk), .Q(x21Out));  // open: clr
  Register #(.width(32)) x24 (.D(WriteData), .en(WE24), .clk(clk), .Q(x24Out));  // open: clr
  Register #(.width(32)) x27 (.D(WriteData), .en(WE27), .clk(clk), .Q(x27Out));  // open: clr
  Register #(.width(32)) x30 (.D(WriteData), .en(WE30), .clk(clk), .Q(x30Out));  // open: clr
  Register #(.width(32)) x3 (.D(WriteData), .en(WE3), .clk(clk), .Q(x3Out));  // open: clr
  Register #(.width(32)) x18 (.D(WriteData), .en(WE18), .clk(clk), .Q(x18Out));  // open: clr
  Demultiplexer #(.select(5)) demultiplexer_1 (
    .out1(WE1), .out2(WE2), .out3(WE3), .out4(WE4), .out5(WE5), .out6(WE6), .out7(WE7), .out8(WE8),
    .out9(WE9), .out10(WE10), .out11(WE11), .out12(WE12), .out13(WE13), .out14(WE14), .out15(WE15),
    .out16(WE16), .out17(WE17), .out18(WE18), .out19(WE19), .out20(WE20), .out21(WE21), .out22(WE22),
    .out23(WE23), .out24(WE24), .out25(WE25), .out26(WE26), .out27(WE27), .out28(WE28), .out29(WE29),
    .out30(WE30), .out31(WE31), .in(RegWEn), .sel(WriteIndex));  // open: out0
  Register #(.width(32)) x1 (.D(WriteData), .en(WE1), .clk(clk), .Q(ra));  // open: clr
  Register #(.width(32)) x7 (.D(WriteData), .en(WE7), .clk(clk), .Q(t2));  // open: clr
  Register #(.width(32)) x10 (.D(WriteData), .en(WE10), .clk(clk), .Q(a0));  // open: clr
  Register #(.width(32)) x13 (.D(WriteData), .en(WE13), .clk(clk), .Q(x13Out));  // open: clr
  Register #(.width(32)) x16 (.D(WriteData), .en(WE16), .clk(clk), .Q(x16Out));  // open: clr
  Register #(.width(32)) x22 (.D(WriteData), .en(WE22), .clk(clk), .Q(x22Out));  // open: clr
  Register #(.width(32)) x25 (.D(WriteData), .en(WE25), .clk(clk), .Q(x25Out));  // open: clr
  Register #(.width(32)) x28 (.D(WriteData), .en(WE28), .clk(clk), .Q(x28Out));  // open: clr
  Register #(.width(32)) x31 (.D(WriteData), .en(WE31), .clk(clk), .Q(x31Out));  // open: clr
  Multiplexer #(.select(5), .width(32)) multiplexer_1 (
    .in0({32{1'b0}}), .in1(ra), .in2(sp), .in3(x3Out), .in4(x4Out), .in5(t0), .in6(t1), .in7(t2), .in8(s0),
    .in9(s1), .in10(a0), .in11(x11Out), .in12(x12Out), .in13(x13Out), .in14(x14Out), .in15(x15Out),
    .in16(x16Out), .in17(x17Out), .in18(x18Out), .in19(x19Out), .in20(x20Out), .in21(x21Out), .in22(x22Out),
    .in23(x23Out), .in24(x24Out), .in25(x25Out), .in26(x26Out), .in27(x27Out), .in28(x28Out), .in29(x29Out),
    .in30(x30Out), .in31(x31Out), .out(ReadData1), .sel(ReadIndex1));
  Register #(.width(32)) x4 (.D(WriteData), .en(WE4), .clk(clk), .Q(x4Out));  // open: clr
  Register #(.width(32)) x19 (.D(WriteData), .en(WE19), .clk(clk), .Q(x19Out));  // open: clr
  Register #(.width(32)) x5 (.D(WriteData), .en(WE5), .clk(clk), .Q(t0));  // open: clr
  Register #(.width(32)) x8 (.D(WriteData), .en(WE8), .clk(clk), .Q(s0));  // open: clr
  Register #(.width(32)) x11 (.D(WriteData), .en(WE11), .clk(clk), .Q(x11Out));  // open: clr
  Register #(.width(32)) x14 (.D(WriteData), .en(WE14), .clk(clk), .Q(x14Out));  // open: clr
  Register #(.width(32)) x20 (.D(WriteData), .en(WE20), .clk(clk), .Q(x20Out));  // open: clr
  Register #(.width(32)) x23 (.D(WriteData), .en(WE23), .clk(clk), .Q(x23Out));  // open: clr
  Register #(.width(32)) x26 (.D(WriteData), .en(WE26), .clk(clk), .Q(x26Out));  // open: clr
  Register #(.width(32)) x29 (.D(WriteData), .en(WE29), .clk(clk), .Q(x29Out));  // open: clr
  Register #(.width(32)) x2 (.D(WriteData), .en(WE2), .clk(clk), .Q(sp));  // open: clr
  Register #(.width(32)) x17 (.D(WriteData), .en(WE17), .clk(clk), .Q(x17Out));  // open: clr
  Multiplexer #(.select(5), .width(32)) multiplexer_2 (
    .in0({32{1'b0}}), .in1(ra), .in2(sp), .in3(x3Out), .in4(x4Out), .in5(t0), .in6(t1), .in7(t2), .in8(s0),
    .in9(s1), .in10(a0), .in11(x11Out), .in12(x12Out), .in13(x13Out), .in14(x14Out), .in15(x15Out),
    .in16(x16Out), .in17(x17Out), .in18(x18Out), .in19(x19Out), .in20(x20Out), .in21(x21Out), .in22(x22Out),
    .in23(x23Out), .in24(x24Out), .in25(x25Out), .in26(x26Out), .in27(x27Out), .in28(x28Out), .in29(x29Out),
    .in30(x30Out), .in31(x31Out), .out(ReadData2), .sel(ReadIndex2));

  // Other names for the same wires on the sheet: x1Out[31:0] = ra; x2Out[31:0] = sp; x5Out[31:0] = t0;
  //   x6Out[31:0] = t1; x7Out[31:0] = t2; x8Out[31:0] = s0; x9Out[31:0] = s1; x10Out[31:0] = a0

  // Notes on the sheet:
  //   INPUTS to your circuit
  //   DON'T CHANGE THE LOCATIONS OF THE INPUTS AND OUTPUTS!
  //   These are DEBUG/TEST outputs from your circuit.
  //   OUTPUTS from your circuit
endmodule
