// Logisim project branch-comp.circ as structural Verilog: 1 circuit, main circuit branch_comp
module branch_comp (
  input  [31:0] BrData1,
  input  [31:0] BrData2,
  input  BrUn,
  output BrEq,
  output BrLt
);

  wire SinEQ, SinLess, UnSinEQ, UnSinLess;

  Comparator #(.width(32)) comparator_1 (.a(BrData1), .b(BrData2), .eq(SinEQ), .lt(SinLess));  // open: gt
  Comparator #(.mode("unsigned"), .width(32)) comparator_2 (
    .a(BrData1), .b(BrData2), .eq(UnSinEQ), .lt(UnSinLess));  // open: gt
  Multiplexer multiplexer_1 (.in0(SinLess), .in1(UnSinLess), .out(BrLt), .sel(BrUn));
  Multiplexer multiplexer_2 (.in0(SinEQ), .in1(UnSinEQ), .out(BrEq), .sel(BrUn));

  // Notes on the sheet:
  //   INPUTS to your circuit
  //   DON'T CHANGE THE LOCATIONS OF THE INPUTS AND OUTPUTS!
  //   OUTPUT from your circuit
endmodule
