// Logisim project control-logic.circ as structural Verilog: 1 circuit, main circuit control_logic
module control_logic (
  input  [31:0] Instruction,
  input  BrEq,
  input  BrLt,
  output PCSel,
  output RegWEn,
  output [2:0] ImmSel,
  output BrUn,
  output ASel,
  output BSel,
  output [3:0] ALUSel,
  output MemWEn,
  output [1:0] WBSel
);

  wire and_31_out, and_32_out, and_33_out, and_34_out, is_000, is_001, is_010, is_011, is_25_0, is_25_1,
       is_30_0, is_30_1, is_100, is_101, is_110, is_111, is_add, is_addi, is_and, is_andi, is_aupic, is_B,
       is_beq, is_bge, is_bgeu, is_blt, is_bltu, is_bne, is_I, is_jal, is_jalr, is_L, is_lb, is_lh, is_lui,
       is_lw, is_mul, is_mulh, is_mulu, is_or, is_ori, is_R, is_S, is_sb, is_sh, is_sll, is_slli, is_slt,
       is_slti, is_sra, is_srai, is_srl, is_srli, is_sub, is_sw, is_xor, is_xori, not_1_out, not_2_out,
       or_1_out, or_2_out;
  wire [5:0] ROMInput;
  wire [15:14] rom_1_data;

  // Priority_Encoder #(.select_enc(6)) priority_encoder_1: pin names not known; wires that end beside it: ROMInput, is_add, is_mul, is_sub, is_sll, is_mulh, is_mulu, is_slt, is_xor, is_srl, is_sra, is_or, is_and, is_lb, is_lh, is_lw, is_addi, is_slli, is_slti, is_xori, is_srli, is_srai, is_ori, is_andi, is_sb, is_sh, is_sw, is_beq, is_bne, is_blt, is_bge, is_bltu, is_bgeu, is_aupic, is_lui, is_jal, is_jalr
  ROM #(.addrWidth(6), .dataWidth(16)) rom_1 (
    .addr(ROMInput), .data({rom_1_data, WBSel, MemWEn, ALUSel, BSel, ASel, BrUn, ImmSel, RegWEn}));
  Comparator #(.mode("unsigned"), .width(7)) comparator_1 (
    .a(Instruction[6:0]), .b(7'b0110011), .eq(is_R));  // open: gt, lt
  Comparator #(.mode("unsigned"), .width(7)) comparator_2 (
    .a(Instruction[6:0]), .b(7'b0000011), .eq(is_L));  // open: gt, lt
  Comparator #(.mode("unsigned"), .width(7)) comparator_3 (
    .a(Instruction[6:0]), .b(7'b0010011), .eq(is_I));  // open: gt, lt
  Comparator #(.mode("unsigned"), .width(7)) comparator_4 (
    .a(Instruction[6:0]), .b(7'b0100011), .eq(is_S));  // open: gt, lt
  Comparator #(.mode("unsigned"), .width(7)) comparator_5 (
    .a(Instruction[6:0]), .b(7'b1100011), .eq(is_B));  // open: gt, lt
  Comparator #(.mode("unsigned"), .width(7)) comparator_6 (
    .a(Instruction[6:0]), .b(7'b0010111), .eq(is_aupic));  // open: gt, lt
  Comparator #(.mode("unsigned"), .width(7)) comparator_7 (
    .a(Instruction[6:0]), .b(7'b0110111), .eq(is_lui));  // open: gt, lt
  Comparator #(.mode("unsigned"), .width(7)) comparator_8 (
    .a(Instruction[6:0]), .b(7'b1101111), .eq(is_jal));  // open: gt, lt
  Comparator #(.mode("unsigned"), .width(7)) comparator_9 (
    .a(Instruction[6:0]), .b(7'b1100111), .eq(is_jalr));  // open: gt, lt
  Comparator #(.mode("unsigned"), .width(3)) comparator_10 (
    .a(Instruction[14:12]), .b(3'b000), .eq(is_000));  // open: gt, lt
  Comparator #(.mode("unsigned"), .width(3)) comparator_11 (
    .a(Instruction[14:12]), .b(3'b001), .eq(is_001));  // open: gt, lt
  Comparator #(.mode("unsigned"), .width(3)) comparator_12 (
    .a(Instruction[14:12]), .b(3'b010), .eq(is_010));  // open: gt, lt
  Comparator #(.mode("unsigned"), .width(3)) comparator_13 (
    .a(Instruction[14:12]), .b(3'b011), .eq(is_011));  // open: gt, lt
  Comparator #(.mode("unsigned"), .width(3)) comparator_14 (
    .a(Instruction[14:12]), .b(3'b100), .eq(is_100));  // open: gt, lt
  Comparator #(.mode("unsigned"), .width(3)) comparator_15 (
    .a(Instruction[14:12]), .b(3'b101), .eq(is_101));  // open: gt, lt
  Comparator #(.mode("unsigned"), .width(3)) comparator_16 (
    .a(Instruction[14:12]), .b(3'b110), .eq(is_110));  // open: gt, lt
  Comparator #(.mode("unsigned"), .width(3)) comparator_17 (
    .a(Instruction[14:12]), .b(3'b111), .eq(is_111));  // open: gt, lt
  and and_1 (is_beq, is_000, is_B);
  and and_2 (is_bne, is_B, is_001);
  and and_3 (is_blt, is_B, is_100);
  and and_4 (is_bge, is_B, is_101);
  and and_5 (is_bltu, is_B, is_110);
  and and_6 (is_bgeu, is_B, is_111);
  and and_7 (is_or, is_110, is_R);
  and and_8 (is_and, is_111, is_R);
  and and_9 (is_lb, is_L, is_000);
  and and_10 (is_lh, is_L, is_001);
  and and_11 (is_lw, is_L, is_010);
  and and_12 (is_addi, is_I, is_000);
  and and_13 (is_slti, is_I, is_010);
  and and_14 (is_ori, is_I, is_110);
  and and_15 (is_sh, is_S, is_001);
  and and_16 (is_sw, is_S, is_010);
  or or_1 (or_1_out, is_bltu, is_blt);
  and and_17 (is_add, is_000, is_30_0, is_25_0, is_R);
  and and_18 (is_mul, is_000, is_000, is_25_1, is_R);
  and and_19 (is_sub, is_000, is_25_0, is_30_1, is_R);
  and and_20 (is_sll, is_001, is_25_0, is_R);
  and and_21 (is_mulh, is_001, is_25_1, is_R);
  and and_22 (is_mulu, is_011, is_R);
  and and_23 (is_slt, is_010, is_R);
  and and_24 (is_xor, is_100, is_R);
  and and_25 (is_srl, is_101, is_30_0, is_R);
  and and_26 (is_sra, is_101, is_30_1, is_R);
  and and_27 (is_sb, is_S, is_000);
  or or_2 (or_2_out, is_bge, is_bgeu);
  Comparator #(.mode("unsigned"), .width(1)) comparator_18 (
    .a(Instruction[25]), .b(1'b0), .eq(is_25_0));  // open: gt, lt
  Comparator #(.mode("unsigned"), .width(1)) comparator_19 (
    .a(Instruction[25]), .b(1'b1), .eq(is_25_1));  // open: gt, lt
  Comparator #(.mode("unsigned"), .width(1)) comparator_20 (
    .a(Instruction[30]), .b(1'b0), .eq(is_30_0));  // open: gt, lt
  Comparator #(.mode("unsigned"), .width(1)) comparator_21 (
    .a(Instruction[30]), .b(1'b1), .eq(is_30_1));  // open: gt, lt
  and and_28 (is_slli, is_001, is_I);
  and and_29 (is_xori, is_I, is_100);
  and and_30 (is_andi, is_I, is_111);
  not not_1 (not_1_out, BrLt);
  and and_31 (and_31_out, is_beq, BrEq);
  not not_2 (not_2_out, BrEq);
  and and_32 (and_32_out, or_1_out, BrLt);
  and and_33 (and_33_out, or_2_out, not_1_out);
  and and_34 (and_34_out, is_bne, not_2_out);
  and and_35 (is_srli, is_30_0, is_I, is_101);
  and and_36 (is_srai, is_I, is_101, is_30_1);
  or or_3 (PCSel, and_31_out, and_34_out, and_32_out, and_33_out, is_jal, is_jalr);

  // Notes on the sheet:
  //   INPUTS to your circuit
  //   Connect ROM Input here ->
  //   contents of rom_1 (hex, n*v repeats v):
  //   101f 141f 161f 109f 149f 159f 111f 121f 129f 169f 131f 139f 5f 5f 5f 1051 10d1 1151 1251 12d1 16d1
  //   1351 13d1 3852 3852 3852 4*3064 3074 3074 1077 17d7 2079 2051
  //   ROM FOR CONTROL LOGIC
  //   DON'T CHANGE THE LOCATIONS OF THE INPUTS AND OUTPUTS!
  //   OUTPUT from your circuit
  //   Reminder: If using ROM, use combinational logic for PCSel
endmodule
