// Logisim project partial-load.circ as structural Verilog: 1 circuit, main circuit partial_load
module partial_load (
  input  [31:0] Instruction,
  input  [31:0] MemAddress,
  input  [31:0] DataFromMem,
  output [31:0] DataToReg
);

  wire [31:0] bit_extender_1_out, bit_extender_2_out, Start, Start8, Start16, Start24;

  assign bit_extender_1_out = {{24{Start[7]}}, Start[7:0]};  // Bit_Extender bit_extender_1
  assign bit_extender_2_out = {{16{Start[15]}}, Start[15:0]};  // Bit_Extender bit_extender_2
  Multiplexer #(.select(2), .width(32)) multiplexer_1 (
    .in0(bit_extender_1_out), .in1(bit_extender_2_out), .in2(Start), .out(DataToReg), .sel(Instruction[13:12]));  // open: in3
  assign Start8 = {{8{DataFromMem[31]}}, DataFromMem[31:8]};  // Bit_Extender bit_extender_3
  assign Start16 = {{16{DataFromMem[31]}}, DataFromMem[31:16]};  // Bit_Extender bit_extender_4
  assign Start24 = {{24{DataFromMem[31]}}, DataFromMem[31:24]};  // Bit_Extender bit_extender_5
  Multiplexer #(.select(2), .width(32)) multiplexer_2 (
    .in0(DataFromMem), .in1(Start8), .in2(Start16), .in3(Start24), .out(Start), .sel(MemAddress[1:0]));

  // Other names for the same wires on the sheet: funct3[1:0] = Instruction[13:12];
  //   Extract_Start[1:0] = MemAddress[1:0]; Start0[31:0] = DataFromMem

  // Notes on the sheet:
  //   INPUTS to your circuit
  //   DON'T CHANGE THE LOCATIONS OF THE INPUTS AND OUTPUTS!
  //   OUTPUT from your circuit
endmodule
