// Logisim project regfile.circ as structural Verilog: 1 circuit, main circuit regfile
module regfile (
  input  [4:0] ReadIndex1,
  input  [4:0] ReadIndex2,
  input  [4:0] WriteIndex,
  input  [31:0] WriteData,
  input  RegWEn,
  input  clk,
  output [31:0] ra,
  output [31:0] sp,
  output [31:0] t0,
  output [31:0] t1,
  output [31:0] t2,
  output [31:0] s0,
  output [31:0] s1,
  output [31:0] a0,
  output [31:0] ReadData1,
  output [31:0] ReadData2
);

  wire comparator_1_eq, comparator_2_eq, comparator_3_eq, comparator_4_eq, comparator_5_eq, comparator_6_eq,
       comparator_7_eq, comparator_8_eq, comparator_9_eq, comparator_10_gt, comparator_11_eq,
       comparator_12_eq, comparator_13_eq, comparator_14_eq, comparator_15_eq, comparator_16_gt,
       comparator_17_eq, comparator_18_eq, comparator_19_gt, comparator_20_eq, comparator_21_eq,
       comparator_22_eq, comparator_23_eq, comparator_24_eq, comparator_25_eq, comparator_26_eq,
       comparator_27_eq, comparator_28_eq, comparator_29_eq, comparator_30_eq, comparator_31_eq, x1Enable,
       x2Enable, x3Enable, x4Enable, x5Enable, x6Enable, x7Enable, x8Enable, x9Enable, x10Enable, x11Enable,
       x12Enable, x13Enable, x14Enable, x15Enable, x16Enable, x17Enable, x18Enable, x19Enable, x20Enable,
       x21Enable, x22Enable, x23Enable, x24Enable, x25Enable, x26Enable, x27Enable, x28Enable, x29Enable,
       x30Enable, x31Enable;
  wire [31:0] undriven, undriven_2, x3Out, x4Out, x7Out, x11Out, x12Out, x13Out, x14Out, x15Out, x16Out,
       x17Out, x18Out, x19Out, x20Out, x21Out, x22Out, x23Out, x24Out, x25Out, x26Out, x27Out, x28Out,
       x29Out, x30Out, x31Out;

  Register #(.width(32)) x6 (.D(WriteData), .en(x6Enable), .clk(clk), .Q(t1));  // open: clr
  Register #(.width(32)) x9 (.D(WriteData), .en(x9Enable), .clk(clk), .Q(s1));  // open: clr
  Register #(.width(32)) x12 (.D(WriteData), .en(x12Enable), .clk(clk), .Q(x12Out));  // open: clr
  Register #(.width(32)) x15 (.D(WriteData), .en(x15Enable), .clk(clk), .Q(x15Out));  // open: clr
  Register #(.width(32)) x21 (.D(WriteData), .en(x21Enable), .clk(clk), .Q(x21Out));  // open: clr
  Register #(.width(32)) x24 (.D(WriteData), .en(x24Enable), .clk(clk), .Q(x24Out));  // open: clr
  Register #(.width(32)) x27 (.D(WriteData), .en(x27Enable), .clk(clk), .Q(x27Out));  // open: clr
  Register #(.width(32)) x30 (.D(WriteData), .en(x30Enable), .clk(clk), .Q(x30Out));  // open: clr
  Register #(.width(32)) x3 (.D(WriteData), .en(x3Enable), .clk(clk), .Q(x3Out));  // open: clr
  Comparator #(.width(5)) comparator_1 (.a(5'b00110), .b(WriteIndex), .eq(comparator_1_eq));  // open: gt, lt
  Comparator #(.width(5)) comparator_2 (.a(5'b01001), .b(WriteIndex), .eq(comparator_2_eq));  // open: gt, lt
  Comparator #(.width(5)) comparator_3 (.a(5'b01100), .b(WriteIndex), .eq(comparator_3_eq));  // open: gt, lt
  Comparator #(.width(5)) comparator_4 (.a(5'b01111), .b(WriteIndex), .eq(comparator_4_eq));  // open: gt, lt
  Register #(.width(32)) x18 (.D(WriteData), .en(x18Enable), .clk(clk), .Q(x18Out));  // open: clr
  Comparator #(.width(5)) comparator_5 (.a(5'b10101), .b(WriteIndex), .eq(comparator_5_eq));  // open: gt, lt
  Comparator #(.width(5)) comparator_6 (.a(5'b11000), .b(WriteIndex), .eq(comparator_6_eq));  // open: gt, lt
  Comparator #(.width(5)) comparator_7 (.a(5'b11100), .b(WriteIndex), .eq(comparator_7_eq));  // open: gt, lt
  Comparator #(.width(5)) comparator_8 (.a({5{1'b1}}), .b(WriteIndex), .eq(comparator_8_eq));  // open: gt, lt
  Comparator #(.width(5)) comparator_9 (.a(5'b00011), .b(WriteIndex), .eq(comparator_9_eq));  // open: gt, lt
  Comparator #(.width(5)) comparator_10 (.a(5'b10010), .b(WriteIndex), .gt(comparator_10_gt));  // open: eq, lt
  and and_1 (x12Enable, comparator_3_eq, RegWEn);
  and and_2 (x24Enable, comparator_6_eq, RegWEn);
  and and_3 (x27Enable, comparator_7_eq, RegWEn);
  and and_4 (x30Enable, comparator_8_eq, RegWEn);
  and and_5 (x3Enable, comparator_9_eq, RegWEn);
  and and_6 (x6Enable, comparator_1_eq, RegWEn);
  and and_7 (x9Enable, comparator_2_eq, RegWEn);
  and and_8 (x15Enable, comparator_4_eq, RegWEn);
  and and_9 (x18Enable, comparator_10_gt, RegWEn);
  and and_10 (x21Enable, comparator_5_eq, RegWEn);
  Register #(.width(32)) x1 (.D(WriteData), .en(x1Enable), .clk(clk), .Q(ra));  // open: clr
  Register #(.width(32)) x7 (.D(WriteData), .en(x7Enable), .clk(clk), .Q(t2));  // open: clr
  Register #(.width(32)) x10 (.D(WriteData), .en(x10Enable), .clk(clk), .Q(a0));  // open: clr
  Register #(.width(32)) x13 (.D(WriteData), .en(x13Enable), .clk(clk), .Q(x13Out));  // open: clr
  Register #(.width(32)) x16 (.D(WriteData), .en(x16Enable), .clk(clk), .Q(x16Out));  // open: clr
  Register #(.width(32)) x22 (.D(WriteData), .en(x22Enable), .clk(clk), .Q(x22Out));  // open: clr
  Register #(.width(32)) x25 (.D(WriteData), .en(x25Enable), .clk(clk), .Q(x25Out));  // open: clr
  Register #(.width(32)) x28 (.D(WriteData), .en(x28Enable), .clk(clk), .Q(x28Out));  // open: clr
  Register #(.width(32)) x31 (.D(WriteData), .en(x31Enable), .clk(clk), .Q(x31Out));  // open: clr
  Multiplexer #(.select(5), .width(32)) multiplexer_1 (
    .in0({32{1'b0}}), .in1(ra), .in2(sp), .in3(x3Out), .in4(x4Out), .in5(t0), .in6(t1), .in7(x7Out),
    .in8(s0), .in9(s1), .in10(a0), .in11(x11Out), .in12(x12Out), .in13(x13Out), .in14(x14Out),
    .in15(undriven), .in16(x16Out), .in17(x17Out), .in18(x18Out), .in19(x19Out), .in20(x20Out),
    .in21(x21Out), .in22(x22Out), .in23(x23Out), .in24(x24Out), .in25(x25Out), .in26(x26Out), .in27(x27Out),
    .in28(x28Out), .in29(x29Out), .in30(x30Out), .in31(x31Out), .out(ReadData1), .sel(ReadIndex1));
  Comparator #(.width(5)) comparator_11 (.a(5'b00001), .b(WriteIndex), .eq(comparator_11_eq));  // open: gt, lt
  Register #(.width(32)) x4 (.D(WriteData), .en(x4Enable), .clk(clk), .Q(x4Out));  // open: clr
  Comparator #(.width(5)) comparator_12 (.a(5'b00111), .b(WriteIndex), .eq(comparator_12_eq));  // open: gt, lt
  Comparator #(.width(5)) comparator_13 (.a(5'b01010), .b(WriteIndex), .eq(comparator_13_eq));  // open: gt, lt
  Comparator #(.width(5)) comparator_14 (.a(5'b01101), .b(WriteIndex), .eq(comparator_14_eq));  // open: gt, lt
  Comparator #(.width(5)) comparator_15 (.a(5'b10000), .b(WriteIndex), .eq(comparator_15_eq));  // open: gt, lt
  Register #(.width(32)) x19 (.D(WriteData), .en(x19Enable), .clk(clk), .Q(x19Out));  // open: clr
  Comparator #(.width(5)) comparator_16 (.a(5'b10110), .b(WriteIndex), .gt(comparator_16_gt));  // open: eq, lt
  Comparator #(.width(5)) comparator_17 (.a(5'b11001), .b(WriteIndex), .eq(comparator_17_eq));  // open: gt, lt
  Comparator #(.width(5)) comparator_18 (.a(5'b11100), .b(WriteIndex), .eq(comparator_18_eq));  // open: gt, lt
  Comparator #(.width(5)) comparator_19 (.a({5{1'b1}}), .b(WriteIndex), .gt(comparator_19_gt));  // open: eq, lt
  Comparator #(.width(5)) comparator_20 (.a(5'b00100), .b(WriteIndex), .eq(comparator_20_eq));  // open: gt, lt
  Comparator #(.width(5)) comparator_21 (.a(5'b10011), .b(WriteIndex), .eq(comparator_21_eq));  // open: gt, lt
  buf and_11 (x1Enable, RegWEn);  // AND_Gate
  and and_12 (x13Enable, comparator_14_eq, RegWEn);
  and and_13 (x25Enable, comparator_17_eq, RegWEn);
  and and_14 (x28Enable, comparator_18_eq, RegWEn);
  and and_15 (x31Enable, comparator_19_gt, RegWEn);
  and and_16 (x4Enable, comparator_20_eq, RegWEn);
  and and_17 (x7Enable, comparator_12_eq, RegWEn);
  and and_18 (x10Enable, comparator_13_eq, RegWEn);
  and and_19 (x16Enable, comparator_15_eq, RegWEn);
  and and_20 (x19Enable, comparator_21_eq, RegWEn);
  and and_21 (x22Enable, comparator_16_gt, RegWEn);
  Register #(.width(32)) x5 (.D(WriteData), .en(x5Enable), .clk(clk), .Q(t0));  // open: clr
  Register #(.width(32)) x8 (.D(WriteData), .en(x8Enable), .clk(clk), .Q(s0));  // open: clr
  Register #(.width(32)) x11 (.D(WriteData), .en(x11Enable), .clk(clk), .Q(x11Out));  // open: clr
  Register #(.width(32)) x14 (.D(WriteData), .en(x14Enable), .clk(clk), .Q(x14Out));  // open: clr
  Register #(.width(32)) x20 (.D(WriteData), .en(x20Enable), .clk(clk), .Q(x20Out));  // open: clr
  Register #(.width(32)) x23 (.D(WriteData), .en(x23Enable), .clk(clk), .Q(x23Out));  // open: clr
  Register #(.width(32)) x26 (.D(WriteData), .en(x26Enable), .clk(clk), .Q(x26Out));  // open: clr
  Register #(.width(32)) x29 (.D(WriteData), .en(x29Enable), .clk(clk), .Q(x29Out));  // open: clr
  Comparator #(.width(5)) comparator_22 (.a(5'b00010), .b(WriteIndex), .eq(comparator_22_eq));  // open: gt, lt
  Register #(.width(32)) x2 (.D(WriteData), .en(x2Enable), .clk(clk), .Q(sp));  // open: clr
  Comparator #(.width(5)) comparator_23 (.a(5'b00101), .b(WriteIndex), .eq(comparator_23_eq));  // open: gt, lt
  Comparator #(.width(5)) comparator_24 (.a(5'b01000), .b(WriteIndex), .eq(comparator_24_eq));  // open: gt, lt
  Comparator #(.width(5)) comparator_25 (.a(5'b01011), .b(WriteIndex), .eq(comparator_25_eq));  // open: gt, lt
  Comparator #(.width(5)) comparator_26 (.a(5'b01110), .b(WriteIndex), .eq(comparator_26_eq));  // open: gt, lt
  Comparator #(.width(5)) comparator_27 (.a(5'b10001), .b(WriteIndex), .eq(comparator_27_eq));  // open: gt, lt
  Register #(.width(32)) x17 (.D(WriteData), .en(x17Enable), .clk(clk), .Q(x17Out));  // open: clr
  Comparator #(.width(5)) comparator_28 (.a(5'b10100), .b(WriteIndex), .eq(comparator_28_eq));  // open: gt, lt
  Comparator #(.width(5)) comparator_29 (.a(5'b10111), .b(WriteIndex), .eq(comparator_29_eq));  // open: gt, lt
  Comparator #(.width(5)) comparator_30 (.a(5'b11010), .b(WriteIndex), .eq(comparator_30_eq));  // open: gt, lt
  Comparator #(.width(5)) comparator_31 (.a(5'b11101), .b(WriteIndex), .eq(comparator_31_eq));  // open: gt, lt
  and and_22 (x8Enable, comparator_24_eq, RegWEn);
  and and_23 (x11Enable, comparator_25_eq, RegWEn);
  and and_24 (x14Enable, comparator_26_eq, RegWEn);
  and and_25 (x17Enable, comparator_27_eq, RegWEn);
  and and_26 (x23Enable, comparator_29_eq, RegWEn);
  and and_27 (x26Enable, comparator_30_eq, RegWEn);
  and and_28 (x29Enable, comparator_31_eq, RegWEn);
  buf and_29 (x2Enable, RegWEn);  // AND_Gate
  and and_30 (x5Enable, comparator_23_eq, RegWEn);
  and and_31 (x20Enable, comparator_28_eq, RegWEn);
  Multiplexer #(.select(5), .width(32)) multiplexer_2 (
    .in0({32{1'b0}}), .in1(ra), .in2(sp), .in3(x3Out), .in4(x4Out), .in5(t0), .in6(t1), .in7(x7Out),
    .in8(s0), .in9(s1), .in10(a0), .in11(x11Out), .in12(x12Out), .in13(x13Out), .in14(x14Out),
    .in15(undriven_2), .in16(x16Out), .in17(x17Out), .in18(x18Out), .in19(x19Out), .in20(x20Out),
    .in21(x21Out), .in22(x22Out), .in23(x23Out), .in24(x24Out), .in25(x25Out), .in26(x26Out), .in27(x27Out),
    .in28(x28Out), .in29(x29Out), .in30(x30Out), .in31(x31Out), .out(ReadData2), .sel(ReadIndex2));

  // Other names for the same wires on the sheet: x1Out[31:0] = ra; x2Out[31:0] = sp; x5Out[31:0] = t0;
  //   x6Out[31:0] = t1; x7out_t[31:0] = t2; x8Out[31:0] = s0; x9Out[31:0] = s1; x10Out[31:0] = a0

  // Notes on the sheet:
  //   INPUTS to your circuit
  //   DON'T CHANGE THE LOCATIONS OF THE INPUTS AND OUTPUTS!
  //   These are DEBUG/TEST outputs from your circuit.
  //   OUTPUTS from your circuit
endmodule
